// Logisim project D flip-flop counter.circ as structural Verilog: 1 circuit, main circuit main
module main (
  output Q3,
  output Q2,
  output Q1,
  output Q0,
  output Q3_2,
  output Q2_2,
  output Q1_2,
  output Q0_2
);

  wire and_1_out, and_2_out, and_3_out, clock_1_out, clock_2_out, d_ff_5_qn, d_ff_6_qn, d_ff_7_qn, d_ff_8_qn,
       xor_1_out, xor_2_out, xor_3_out, xor_4_out;

  and and_1 (and_1_out, 1'b1, Q0);
  and and_2 (and_2_out, and_1_out, Q1);
  and and_3 (and_3_out, and_2_out, Q2);
  Clock clock_1 (.out(clock_1_out));
  xor xor_1 (xor_1_out, Q0, 1'b1);
  xor xor_2 (xor_2_out, Q1, and_1_out);
  xor xor_3 (xor_3_out, Q2, and_2_out);
  xor xor_4 (xor_4_out, Q3, and_3_out);
  D_Flip_Flop d_ff_1 (.clk(clock_2_out), .D(xor_1_out), .Q(Q0));  // open: Qn, preset, en, reset
  D_Flip_Flop d_ff_2 (.clk(clock_2_out), .D(xor_2_out), .Q(Q1));  // open: Qn, preset, en, reset
  D_Flip_Flop d_ff_3 (.clk(clock_2_out), .D(xor_3_out), .Q(Q2));  // open: Qn, preset, en, reset
  D_Flip_Flop d_ff_4 (.clk(clock_2_out), .D(xor_4_out), .Q(Q3));  // open: Qn, preset, en, reset
  D_Flip_Flop d_ff_5 (.clk(clock_1_out), .D(d_ff_5_qn), .Q(Q0_2), .Qn(d_ff_5_qn));  // open: preset, en, reset
  D_Flip_Flop d_ff_6 (.clk(d_ff_5_qn), .D(d_ff_6_qn), .Q(Q1_2), .Qn(d_ff_6_qn));  // open: preset, en, reset
  D_Flip_Flop d_ff_7 (.clk(d_ff_6_qn), .D(d_ff_7_qn), .Q(Q2_2), .Qn(d_ff_7_qn));  // open: preset, en, reset
  D_Flip_Flop d_ff_8 (.clk(d_ff_7_qn), .D(d_ff_8_qn), .Q(Q3_2), .Qn(d_ff_8_qn));  // open: preset, en, reset
  Clock clock_2 (.out(clock_2_out));
endmodule
