// Logisim project D-JK flip-flop 3 bit counter.circ as structural Verilog: 1 circuit, main circuit main
module main (
  output Q2,
  output Q1,
  output Q0,
  output Q2_2,
  output Q1_2,
  output Q0_2
);

  wire clock_1_out, clock_2_out, d_ff_1_qn, d_ff_2_qn, d_ff_3_qn, j_k_ff_1_qn, j_k_ff_2_qn, j_k_ff_3_qn,
       not_1_out, not_2_out, not_3_out;

  Clock clock_1 (.out(clock_1_out));
  Clock clock_2 (.out(clock_2_out));
  not not_1 (not_1_out, j_k_ff_1_qn);
  not not_2 (not_2_out, j_k_ff_2_qn);
  not not_3 (not_3_out, j_k_ff_3_qn);
  J_K_Flip_Flop j_k_ff_1 (
    .J(j_k_ff_1_qn), .clk(clock_1_out), .K(not_1_out), .Q(Q0), .Qn(j_k_ff_1_qn));  // open: preset, en, reset
  J_K_Flip_Flop j_k_ff_2 (
    .J(j_k_ff_2_qn), .clk(j_k_ff_1_qn), .K(not_2_out), .Q(Q1), .Qn(j_k_ff_2_qn));  // open: preset, en, reset
  J_K_Flip_Flop j_k_ff_3 (
    .J(j_k_ff_3_qn), .clk(j_k_ff_2_qn), .K(not_3_out), .Q(Q2), .Qn(j_k_ff_3_qn));  // open: preset, en, reset
  D_Flip_Flop #(.trigger("falling")) d_ff_1 (
    .clk(clock_2_out), .D(d_ff_1_qn), .Q(Q0_2), .Qn(d_ff_1_qn));  // open: preset, en, reset
  D_Flip_Flop #(.trigger("falling")) d_ff_2 (
    .clk(d_ff_1_qn), .D(d_ff_2_qn), .Q(Q1_2), .Qn(d_ff_2_qn));  // open: preset, en, reset
  D_Flip_Flop #(.trigger("falling")) d_ff_3 (
    .clk(d_ff_2_qn), .D(d_ff_3_qn), .Q(Q2_2), .Qn(d_ff_3_qn));  // open: preset, en, reset
endmodule
