// Logisim project T-JK flip-flop 3 bit counter.circ as structural Verilog: 1 circuit, main circuit main
module main (
  output Q2,
  output Q0,
  output Q1,
  output Q2_2,
  output Q1_2,
  output Q0_2
);

  wire and_1_out, clock_1_out, clock_2_out, j_k_ff_1_qn, j_k_ff_5_qn;

  Clock clock_1 (.out(clock_1_out));
  Clock clock_2 (.out(clock_2_out));
  J_K_Flip_Flop j_k_ff_1 (
    .J(1'b1), .clk(clock_1_out), .K(1'b1), .Q(Q0_2), .Qn(j_k_ff_1_qn));  // open: preset, en, reset
  J_K_Flip_Flop j_k_ff_2 (.J(1'b1), .clk(clock_2_out), .K(1'b1), .Q(Q0));  // open: Qn, preset, en, reset
  J_K_Flip_Flop j_k_ff_3 (.J(Q0), .clk(clock_2_out), .K(Q0), .Q(Q1));  // open: Qn, preset, en, reset
  J_K_Flip_Flop j_k_ff_4 (.J(and_1_out), .clk(clock_2_out), .K(and_1_out), .Q(Q2));  // open: Qn, preset, en, reset
  J_K_Flip_Flop j_k_ff_5 (
    .J(1'b1), .clk(j_k_ff_1_qn), .K(1'b1), .Q(Q1_2), .Qn(j_k_ff_5_qn));  // open: preset, en, reset
  and and_1 (and_1_out, Q0, Q1);
  J_K_Flip_Flop j_k_ff_6 (.J(1'b1), .clk(j_k_ff_5_qn), .K(1'b1), .Q(Q2_2));  // open: Qn, preset, en, reset
endmodule
